// Logisim project and gates.circ as structural Verilog
module main (
  input  [15:0] A,
  input  [15:0] B,
  output [15:0] S
);

  and and_1 (S[0], A[0], B[0]);
  and and_2 (S[1], A[1], B[1]);
  and and_3 (S[2], A[2], B[2]);
  and and_4 (S[3], A[3], B[3]);
  and and_5 (S[4], A[4], B[4]);
  and and_6 (S[5], A[5], B[5]);
  and and_7 (S[6], A[6], B[6]);
  and and_8 (S[7], A[7], B[7]);
  and and_9 (S[8], A[8], B[8]);
  and and_10 (S[9], A[9], B[9]);
  and and_11 (S[10], A[10], B[10]);
  and and_12 (S[11], A[11], B[11]);
  and and_13 (S[12], A[12], B[12]);
  and and_14 (S[13], A[13], B[13]);
  and and_15 (S[14], A[14], B[14]);
  and and_16 (S[15], A[15], B[15]);

  // Notes on the sheet:
  //   S: pull=down
endmodule
